# Fritzing sketch StrikeAndDip (saved by Fritzing 0.9.3b)
circuit board: 8.24678cm x 5.9999cm
breadboards: 1

parts:
  GPS = Adafruit Ultimate GPS v3 [part_number="Adafruit #746"]
  Altimeter = MPL3115A2 I2C Barometric Pressure, Altitude, Temperature Sensor
  9DOF = Adafruit LSM9DS1 9DoF Breakout [part_number="Adafruit #3387"]
  part = Adafruit Feather M0 Adalogger [part_number="Adafruit #2796"]

nets:
  GND: GPS.GND, Altimeter.GND, 9DOF.GND, part.GND
  N1: GPS.RX, part.D1
  N2: GPS.TX, part.D0
  +3V3: GPS.3.3V, Altimeter.+3V3, 9DOF.VIN, part.+3V3
  N3: Altimeter.SCL, 9DOF.SCL, part.SCL
  N4: Altimeter.SDA, 9DOF.SDA, part.SDA

custom parts:
  Adafruit Ultimate GPS v3: We carry a few different GPS modules here in the Adafruit shop, but none that satisfied our every desire - that's why we designed this little GPS breakout board. We believe this is the Ultimate GPS module, so we named it that. It's got everything you want and more: -165 dBm sensitivity, 10 Hz updates, 66 channels 5V friendly design and only 20mA current draw Breadboard friendly + two mounting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
  MPL3115A2 I2C Barometric Pressure, Altitude, Temperature Sensor: This pressure sensor from Freescale is a great low-cost sensing solution for precision measurement of barometric pressure and altitude. The MPL3115A2 has a typical 1.5 Pascal resolution, which can resolve altitude at 0.3 meters (compare to the BMP180 which can do 0.17m). It has some upsides compared to the BMP180, such as interrupt outputs for ultra-low power usage, and its also a heck of a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
  Adafruit LSM9DS1 9DoF Breakout: Add motion, direction and orientation sensing to your Arduino project with this all-in-one 9-DOF sensor. Inside the chip are three sensors, one is a classic 3-axis accelerometer, which can tell you which direction is down towards the Earth (by measuring gravity) or how fast the board is accelerating in 3D space. The other is a 3-axis magnetometer that can sense where the strongest magnetic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
  Adafruit Feather M0 Adalogger: This is the Adafruit Feather M0 Adalogger - our take on an 'all-in-one' Cortex M0 datalogger (or data-reader) with built in USB and battery charging. Its an Adafruit Feather M0 with a microSD holder ready to rock! We have other boards in the Feather family, check'em out here At the Feather M0's heart is an ATSAMD21G18 ARM Cortex M0 processor, clocked at 48 MHz and at 3.3V logic, the same one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
